# Fritzing sketch van_tay (saved by Fritzing 0.9.9b)

parts:
  Linh_kiện1 = Arduino Nano (Rev3.0)
  Linh_kiện2 = sensor_biometrico
  Raspberry_Pi_1 = Raspberry Pi 3 [part_number=RPI-3-V1.2]
  LCM1602_IIC1 = LCM1602 IIC [part_number="LCM1602 IIC" chip_label="LCM1602 IIC" package="DIP (Dual Inline) [THT]"]
  LCD1 = LCD screen
  S1 = Pushbutton [package=THT]
  S2 = Pushbutton [package=THT]
  J1 = Piezo Speaker
  M1 = 1 chan 5v relay module

nets:
  GND: Linh_kiện1.GND, Linh_kiện2.GND, Raspberry_Pi_1.GND, LCM1602_IIC1.GND, S1.leg0, S2.leg0, J1.pin1, M1.pin_2
  N1: Linh_kiện1.D2, Linh_kiện2.TX
  N2: Linh_kiện1.D3, Linh_kiện2.RX
  N3: Linh_kiện1.D4, Raspberry_Pi_1.GIPO14
  N4: Linh_kiện1.D5, Raspberry_Pi_1.GIPO15
  VIN: Linh_kiện1.VIN, Raspberry_Pi_1.5V, LCM1602_IIC1.VCC, M1.pin_1
  3V3: Linh_kiện1.3V3, Linh_kiện2.VCC
  N5: Raspberry_Pi_1.GPIO2, LCM1602_IIC1.SDA
  N6: Raspberry_Pi_1.GPIO3, LCM1602_IIC1.SCL
  N7: Raspberry_Pi_1.GIPO5, S2.leg1
  N8: Raspberry_Pi_1.GIPO6, J1.pin2
  N9: Raspberry_Pi_1.GIPO26, S1.leg1
  N10: Raspberry_Pi_1.GIPO23, M1.pin_3
  VSS: LCM1602_IIC1.VSS, LCD1.VSS
  VDD: LCM1602_IIC1.VDD, LCD1.VDD
  N11: LCM1602_IIC1.V0, LCD1.V0
  N12: LCM1602_IIC1.RS, LCD1.RS
  N13: LCM1602_IIC1.RW, LCD1.R/W
  N14: LCM1602_IIC1.E, LCD1.E
  N15: LCM1602_IIC1.D0, LCD1.DB0
  N16: LCM1602_IIC1.D1, LCD1.DB1
  N17: LCM1602_IIC1.D2, LCD1.DB2
  N18: LCM1602_IIC1.D3, LCD1.DB3
  N19: LCM1602_IIC1.D4, LCD1.DB4
  N20: LCM1602_IIC1.D5, LCD1.DB5
  N21: LCM1602_IIC1.D6, LCD1.DB6
  N22: LCM1602_IIC1.D7, LCD1.DB7
  N23: LCM1602_IIC1.A, LCD1.LED+
  N24: LCM1602_IIC1.K, LCD1.LED-

custom parts:
  sensor_biometrico: Adafruit Optical Fingerprint Sensor
  LCM1602 IIC: I2C-Module to use a 1602 or 2004 LCD on with the wire.h libory Serial LCD Modul
  1 chan 5v relay module: 1 Channel 5V Relay Module Board Shield with Optocoupler Support High and Low Level Trigger for Arduino.
